# Fritzing sketch MonsterShield_PROD_0.1B_001 (saved by Fritzing 0.7.5b)
breadboards: 2

parts:
  MonsterShield = Arduino
  S1 = Pushbutton [package="[THT]"]
  S2 = Pushbutton [package="[THT]"]
  J4_Audio = Stereo Jack (TRS) 3.5mm [package="PG203J [THT]"]
  J1 = screw terminal, 3 pins
  24LC256 = 24LC256 [package=THT]
  Keypad = RJ45
  LED1 = smd LED [color="Red (633nm)" package="0805 [SMD]"]
  S3 = Pushbutton [package="[THT]"]
  MCP23017 = SSOP28DB [chip_label=MCP23017 spacing=300mil package=SSOP]
  C1 = Ceramic Capacitor [capacitance=0.1µF package="0603 [SMD, multilayer]"]
  R3 = Resistor [tolerance=±5% resistance=1k package="0603 [SMD]"]
  C2 = Ceramic Capacitor [capacitance=0.1µF package="0603 [SMD, multilayer]"]
  C3 = Ceramic Capacitor [capacitance=0.1µF package="0603 [SMD, multilayer]"]
  R1 = Resistor [tolerance=±5% resistance=4.7k package="0603 [SMD]"]
  R13 = Resistor [tolerance=±5% resistance=150 package="0603 [SMD]"]
  R14 = Resistor [tolerance=±5% resistance=150 package="0603 [SMD]"]
  R15 = Resistor [tolerance=±5% resistance=150 package="0603 [SMD]"]
  R16 = Resistor [tolerance=±5% resistance=150 package="0603 [SMD]"]
  R2 = Resistor [tolerance=±5% resistance=4.7k package="0603 [SMD]"]
  R9 = Resistor [tolerance=±5% resistance=150 package="0603 [SMD]"]
  R10 = Resistor [tolerance=±5% resistance=150 package="0603 [SMD]"]
  R11 = Resistor [tolerance=±5% resistance=150 package="0603 [SMD]"]
  R12 = Resistor [tolerance=±5% resistance=150 package="0603 [SMD]"]
  R7 = Resistor [tolerance=±5% resistance=150 package="0603 [SMD]"]
  R4 = Resistor [tolerance=±5% resistance=10k package="0603 [SMD]"]
  R5 = Resistor [tolerance=±5% resistance=10k package="0603 [SMD]"]
  R6 = Resistor [tolerance=±5% resistance=10k package="0603 [SMD]"]
  LED2 = smd LED [color="Orange (620nm)" package="0805 [SMD]"]
  R8 = Resistor [tolerance=±5% resistance=150 package="0603 [SMD]"]
  J3_MP3_Module = female pin header, 20 pins [form="♀ (female)"]
  J2_Relays = male pin header, 6 pins [form="♂ (male)"]
  7_Segment = 7 Segment Display
  S4 = Pushbutton [package="[THT]"]
  R17 = Resistor [tolerance=±5% resistance=10k package="0603 [SMD]"]

nets:
  N1: MonsterShield.GND, J4_Audio.Sleeve, J1.pin3, 24LC256.A0, 24LC256.A1, 24LC256.0V, Keypad.pin_1, LED1.anode, MCP23017.10, MCP23017.15, MCP23017.16, MCP23017.17, C1.1, C2.0, C3.1, R4.Pin_1, R5.Pin_1, R6.Pin_1, R8.Pin_1, J3_MP3_Module.pin19, J2_Relays.pin1, 7_Segment.Segment_A#1, 7_Segment.Segment_DP, R17.Pin_1
  N2: MonsterShield.D13, LED2.cathode
  N3: MonsterShield.D12, Keypad.pin_2
  N4: MonsterShield.D11, Keypad.pin_4
  N5: MonsterShield.D10, Keypad.pin_6
  N6: MonsterShield.D9, Keypad.pin_5
  N7: MonsterShield.D8, Keypad.pin_3
  N8: MonsterShield.D7, Keypad.pin_7
  N9: MonsterShield.D3, J3_MP3_Module.pin15
  N10: MonsterShield.RST, S4.Pin_3, S4.Pin_4
  N11: MonsterShield.+5V, S1.Pin_3, S1.Pin_4, S2.Pin_3, S2.Pin_4, J1.pin1, 24LC256.A2, 24LC256.+V, Keypad.pin_8, S3.Pin_3, S3.Pin_4, MCP23017.9, C1.0, R3.Pin_1, C2.1, C3.0, R1.Pin_1, R2.Pin_1, J3_MP3_Module.pin20, J2_Relays.pin6
  N12: MonsterShield.A0, J1.pin2
  N13: MonsterShield.A4, 24LC256.SDA_-_I2C_Data, MCP23017.13, R2.Pin_0
  N14: MonsterShield.A5, 24LC256.SCL_-_I2C_Clock, MCP23017.12, R1.Pin_0
  N15: S1.Pin_1, S1.Pin_2, MCP23017.28, R4.Pin_0
  N16: S2.Pin_1, S2.Pin_2, MCP23017.27, R5.Pin_0
  N17: J4_Audio.Ring, J3_MP3_Module.pin17
  N18: J4_Audio.Tip, J3_MP3_Module.pin18
  N19: LED1.cathode, R7.Pin_0
  N20: S3.Pin_1, S3.Pin_2, MCP23017.26, R6.Pin_0
  N21: MCP23017.1, R9.Pin_0
  N22: MCP23017.2, R10.Pin_0
  N23: MCP23017.3, R11.Pin_0
  N24: MCP23017.4, R12.Pin_0
  N25: MCP23017.5, R16.Pin_0
  N26: MCP23017.6, R15.Pin_0
  N27: MCP23017.7, R14.Pin_0
  N28: MCP23017.8, R13.Pin_0
  N29: MCP23017.18, R3.Pin_0
  N30: MCP23017.21, J2_Relays.pin2
  N31: MCP23017.22, J2_Relays.pin3
  N32: MCP23017.23, J2_Relays.pin4
  N33: MCP23017.24, J2_Relays.pin5
  N34: MCP23017.25, R7.Pin_1
  N35: R13.Pin_1, 7_Segment.Segment_C
  N36: R14.Pin_1, 7_Segment.common_cathode#8
  N37: R15.Pin_1, 7_Segment.Segment_B
  N38: R16.Pin_1, 7_Segment.Segment_A#10
  N39: R9.Pin_1, 7_Segment.Segment_D
  N40: R10.Pin_1, 7_Segment.Segment_E
  N41: R11.Pin_1, 7_Segment.common_cathode#3
  N42: R12.Pin_1, 7_Segment.Segment_F
  N43: LED2.anode, R8.Pin_0
  N44: S4.Pin_1, S4.Pin_2, R17.Pin_0

notes:
  5V+
  GND
  REV 0.1B
  (c) 2012 HauntSoft
  reset
  nxt/ambient
  prev/enable
  mode/trigger
  Trigger
