# Fritzing sketch keypad_V2 (saved by Fritzing 0.7.5b)
breadboards: 1

parts:
  RJ45 = RJ45
  S1 = Pushbutton [package="[THT]"]
  S2 = Pushbutton [package="[THT]"]
  S3 = Pushbutton [package="[THT]"]
  S4 = Pushbutton [package="[THT]"]
  S5 = Pushbutton [package="[THT]"]

nets:
  N1: RJ45.pin_1, S1.Pin_1, S1.Pin_2, S2.Pin_1, S2.Pin_2, S3.Pin_1, S3.Pin_2, S4.Pin_1, S4.Pin_2, S5.Pin_1, S5.Pin_2
  N2: RJ45.pin_2, S1.Pin_3, S1.Pin_4
  N3: RJ45.pin_3, S5.Pin_3, S5.Pin_4
  N4: RJ45.pin_4, S2.Pin_3, S2.Pin_4
  N5: RJ45.pin_5, S4.Pin_3, S4.Pin_4
  N6: RJ45.pin_6, S3.Pin_3, S3.Pin_4

notes:
  Record
  Out 1
  Out 2
  Out 3
  Out 4
  Prev
  Next
  Enable
  Play/Stop
